// Logisim project micro.circ as structural Verilog: 1 circuit, main circuit EV20_Superescalar
module EV20_Superescalar (
);

  wire button_1_out, CLK, CLK2, CLK3, CLK4, dipswitch_1_sw1, not_1_out, not_2_out, not_3_out,
       pipeline_register_3_p11, pipeline_register_3_p12, selector_a_1_p2, undriven, undriven_2, undriven_3,
       undriven_4;
  wire [5:0] selector_c_1_busc_selector;
  wire [10:0] ProgramCounterReg_ia0ia10;
  wire [14:0] MicroInstructionROM_microinstruction;
  wire [23:0] InstructionRegister_q, ProgramMemory_data;

  ROM #(.addrWidth(11), .dataWidth(24)) ProgramMemory (.addr(ProgramCounterReg_ia0ia10), .data(ProgramMemory_data));
  DipSwitch #(.number(2)) dipswitch_1 (.sw1(dipswitch_1_sw1));  // open: sw2
  Button button_1 (.out(button_1_out));
  PCreg ProgramCounterReg (.HOLD(undriven), .IA0IA10(ProgramCounterReg_ia0ia10));  // open: Preload, CLK1, B0B10
  ClockGenerator clocks (
    .Auto(dipswitch_1_sw1), .ManualCLK(button_1_out), .CLK(CLK), .CLK2(CLK2), .CLK3(CLK3), .CLK4(CLK4));
  Register #(.width(24)) InstructionRegister (
    .D(ProgramMemory_data), .en(undriven), .Q(InstructionRegister_q));  // open: clk, clr
  Register #(.width(16)) BusB_ALU (.D(16'hcccc));  // open: en, clk, Q, clr
  not not_1 (not_1_out, undriven_2);
  // ALU ALUALULAU: pin names not known
  Pipeline_register pipeline_register_1 (
    .S_low_P_high(1'b0), .Hold(not_1_out));  // open: ALUC_IN, SH_IN, Kmx_IN, CLK, MRyMB_IN, B_bus_IN, T_bus_IN, C_bus_IN, Serial_IN, A_bus_IN, D_Address_IN, ALUC_OUT, SH_OUT, Kmx_OUT, MRyMB_OUT, B_bus_OUT, T_bus_OUT, C_bus_OUT, Serial_OUT, A_bus_OUT, D_Address_OUT
  Register #(.width(16)) BusA_ALU (.D(16'hbbbb));  // open: en, clk, Q, clr
  not not_2 (not_2_out, undriven_3);
  // Selector_A selector_a_1: pin names not known; wires that end beside it: InstructionRegister_q, selector_a_1_p2
  Selector_C selector_c_1 (.BusB(InstructionRegister_q), .BusC_Selector(selector_c_1_busc_selector));
  Micro_Instruction_ROM MicroInstructionROM (
    .Instruction(InstructionRegister_q), .MicroInstruction(MicroInstructionROM_microinstruction));
  Pipeline_register pipeline_register_2 (
    .S_low_P_high(1'b0), .Hold(not_2_out));  // open: ALUC_IN, SH_IN, Kmx_IN, CLK, MRyMB_IN, B_bus_IN, T_bus_IN, C_bus_IN, Serial_IN, A_bus_IN, D_Address_IN, ALUC_OUT, SH_OUT, Kmx_OUT, MRyMB_OUT, B_bus_OUT, T_bus_OUT, C_bus_OUT, Serial_OUT, A_bus_OUT, D_Address_OUT
  // Pipeline_register pipeline_register_3: pin names not known; wires that end beside it: MicroInstructionROM_microinstruction[14:11], MicroInstructionROM_microinstruction[10:9], MicroInstructionROM_microinstruction[8], 1'b1, MicroInstructionROM_microinstruction[7:6], InstructionRegister_q[14:10], MicroInstructionROM_microinstruction[5:0], selector_c_1_busc_selector, selector_a_1_p2, InstructionRegister_q[14:5], pipeline_register_3_p11, pipeline_register_3_p12
  not not_3 (not_3_out, undriven_4);
  Register #(.width(16)) BusA_LS (.D(16'haaaa));  // open: en, clk, Q, clr
  // UC1 uc1_1: pin names not known; wires that end beside it: pipeline_register_3_p11, pipeline_register_3_p12
  Pipeline_register LoadStore (
    .S_low_P_high(1'b0), .Hold(not_3_out));  // open: ALUC_IN, SH_IN, Kmx_IN, CLK, MRyMB_IN, B_bus_IN, T_bus_IN, C_bus_IN, Serial_IN, A_bus_IN, D_Address_IN, ALUC_OUT, SH_OUT, Kmx_OUT, MRyMB_OUT, B_bus_OUT, T_bus_OUT, C_bus_OUT, Serial_OUT, A_bus_OUT, D_Address_OUT

  // Notes on the sheet:
  //   BUS B
endmodule
